# Fritzing sketch DiagramaEquipo3 (saved by Fritzing 0.9.3b)
breadboards: 1

parts:
  Componente1 = Arduino Uno (Rev3) - ICSP
  R1 = Resistor [tolerance=±5% resistance=220 package="2512 [SMD]"]
  Q1 = TRANSISTOR_NPN [package=to-92]
  M1 = DC Motor

nets:
  N1: Componente1.D2, R1.Pin_1, Q1.C
  N2: Componente1.5V, R1.Pin_0, Q1.E, M1.pin_1
  N3: Componente1.GND, Q1.B, M1.pin_2
